# Fritzing sketch ejercicio_1_diagrama (saved by Fritzing 0.9.3b)
breadboards: 1

parts:
  Arduino_1 = Arduino Uno (Rev3)
  LED1 = smd LED [color="Red (633nm)" package="0603 [SMD]"]
  R1 = Resistor [tolerance=±5% resistance=220 package="1206 [SMD]"]

nets:
  N1: Arduino_1.D12/MISO, R1.Pin_0
  N2: Arduino_1.GND, LED1.cathode
  N3: LED1.anode, R1.Pin_1
