# Fritzing sketch ejercicio_2_diagrama (saved by Fritzing 0.9.3b)
breadboards: 1

parts:
  Arduino_uno = Arduino Uno (Rev3)
  R2 = Resistor [tolerance=±5% resistance=220 package="1206 [SMD]"]
  LED2 = smd LED [color="Red (633nm)" package="0603 [SMD]"]
  switch = Momentary Switch [package=ksa_sealed_tac_switch]
  R3 = Resistor [tolerance=±5% resistance=1k package="0603 [SMD]"]

nets:
  N1: Arduino_uno.D12/MISO, R2.Pin_0
  N2: Arduino_uno.GND, LED2.cathode, R3.Pin_1
  N3: Arduino_uno.D4, switch.1, R3.Pin_0
  N4: Arduino_uno.5V, switch.3
  N5: R2.Pin_1, LED2.anode
