# Fritzing sketch ejercicio_3_diagrama (saved by Fritzing 0.9.3b)
breadboards: 1

parts:
  Arduino_uno = Arduino Uno (Rev3)
  R2 = Resistor [tolerance=±5% resistance=220 package="1206 [SMD]"]
  LED2 = smd LED [color="Red (633nm)" package="0603 [SMD]"]
  YL-56 = Sound Sensor

nets:
  N1: Arduino_uno.D12/MISO, R2.Pin_0
  GND: Arduino_uno.GND, LED2.cathode, YL-56.GND
  N2: Arduino_uno.D3_PWM, YL-56.OUT
  5V: Arduino_uno.5V, YL-56.VCC
  N3: R2.Pin_1, LED2.anode
